# Fritzing sketch projekt_skps (saved by Fritzing 0.9.3b)
breadboards: 1

parts:
  Mod1 = Raspberry Pi 4B
  J1 = Basic Servo
  Part1 = LCD1602-I2C
  S1 = Pushbutton [package="[THT]"]
  S2 = Pushbutton [package="[THT]"]

nets:
  VCC: Mod1.5V, J1.vcc, Part1.VCC
  GND: Mod1.GND, Mod1.GPIO6, Mod1.GPIO13, J1.gnd, Part1.GND, S1.Pin_1, S1.Pin_2, S1.Pin_3, S1.Pin_4, S2.Pin_1, S2.Pin_2, S2.Pin_3, S2.Pin_4
  N1: Mod1.GPIO25, Part1.SDA
  N2: Mod1.GPIO8, Part1.SCL

custom parts:
  LCD1602-I2C: A standard character display, usually with 2x16 characters. Comes in many colors with LCM1602 IIC attached.
