# Fritzing sketch lab5 (saved by Fritzing 0.9.3b)
breadboards: 1

parts:
  Mod1 = Raspberry Pi 4B
  Part1 = LCD1602-I2C
  LED1 = LED - 3mm [color="Red (633nm)" package="3 mm [THT]"]
  Part2 = Logic Level Converter
  R1 = Resistor [tolerance=±5% resistance=220 package="2512 [SMD]"]
  Keypad4x2 = Keypad Membran 4x4
  R2 = Resistor [tolerance=±5% resistance=220 package="2512 [SMD]"]

nets:
  N1: Mod1.3V3, Part2.LV
  5V: Mod1.5V, Part1.VCC, Part2.HV
  N2: Mod1.GPIO2, Part2.TX2_HV
  N3: Mod1.GPIO3, Part2.RX2_HV
  GND: Mod1.GND, Part1.GND, Part2.GND, R1.Pin_0, R2.Pin_1
  N4: Mod1.GPIO18, LED1.anode
  N5: Mod1.GPIO6, Keypad4x2.Pin8
  N6: Part1.SDA, Part2.TX2_LV
  N7: Part1.SCL, Part2.RX2_LV
  N8: LED1.cathode, R1.Pin_1
  N9: Keypad4x2.Pin4, R2.Pin_0

notes:
  5V
  3.3V

custom parts:
  LCD1602-I2C: A standard character display, usually with 2x16 characters. Comes in many colors with LCM1602 IIC attached.
  Keypad Membran 4x4: Membrane Keypad 4x4 Matrix
