# Fritzing sketch lab5 (saved by Fritzing 0.9.3b)
breadboards: 1

parts:
  Mod1 = Raspberry Pi 4B
  Part1 = LCD1602-I2C
  LED1 = LED - 3mm [color="Red (633nm)" package="3 mm [THT]"]
  Part2 = Logic Level Converter
  R1 = Resistor [tolerance=±5% resistance=220 package="2512 [SMD]"]
  Keypad4x2 = Keypad Membran 4x4
  R2 = Resistor [tolerance=±5% resistance=220 package="2512 [SMD]"]
  R3 = Resistor [tolerance=±5% resistance=220 package="2512 [SMD]"]
  LED2 = LED - 3mm [color="Green (560nm)" package="3 mm [THT]"]
  R4 = Resistor [tolerance=±5% resistance=220 package="2512 [SMD]"]
  R5 = Resistor [tolerance=±5% resistance=220 package="2512 [SMD]"]
  R7 = Resistor [tolerance=±5% resistance=220 package="2512 [SMD]"]
  R8 = Resistor [tolerance=±5% resistance=220 package="2512 [SMD]"]
  R9 = Resistor [tolerance=±5% resistance=220 package="2512 [SMD]"]
  J1 = Basic Servo

nets:
  N1: Mod1.3V3, Part2.LV, R3.Pin_0, R4.Pin_0, R5.Pin_0
  VCC: Mod1.5V, Part1.VCC, Part2.HV, J1.vcc
  N2: Mod1.GPIO2, Part2.TX_LV
  N3: Mod1.GPIO3, Part2.RX_LV
  GND: Mod1.GND, Part1.GND, Part2.GND, R1.Pin_0, Keypad4x2.Pin5, R9.Pin_0, J1.gnd
  N4: Mod1.GPIO18, LED1.anode, J1.pulse
  N5: Mod1.GPIO5, LED2.anode
  N6: Mod1.GPIO6, R2.Pin_1
  N7: Mod1.GPIO19, R8.Pin_1
  N8: Mod1.GPIO26, R7.Pin_1
  N9: Part1.SDA, Part2.TX_HV
  N10: Part1.SCL, Part2.RX_HV
  N11: LED1.cathode, R1.Pin_1
  N12: Keypad4x2.Pin1, R3.Pin_1, R7.Pin_0
  N13: Keypad4x2.Pin2, R4.Pin_1, R8.Pin_0
  N14: Keypad4x2.Pin3, R2.Pin_0, R5.Pin_1
  N15: LED2.cathode, R9.Pin_1

notes:
  5V
  3.3V

custom parts:
  LCD1602-I2C: A standard character display, usually with 2x16 characters. Comes in many colors with LCM1602 IIC attached.
  Keypad Membran 4x4: Membrane Keypad 4x4 Matrix
