# Fritzing sketch project_scheme (saved by Fritzing 0.9.9b)
breadboards: 1

parts:
  Mod1 = Raspberry Pi 4B
  Part1 = LCD1602-I2C
  LED1 = LED - 3mm [color="Red (633nm)" current=0.030 package="3 mm [THT]"]
  Part2 = Logic Level Converter
  R1 = Resistor [tolerance=±5% resistance=220 package="2512 [SMD]"]
  R2 = Resistor [tolerance=±5% resistance=220 package="2512 [SMD]"]
  LED2 = LED - 3mm [color="Green (560nm)" current=0.030 package="3 mm [THT]"]
  R7 = Resistor [tolerance=±5% resistance=220 package="2512 [SMD]"]
  R8 = Resistor [tolerance=±5% resistance=220 package="2512 [SMD]"]
  R9 = Resistor [tolerance=±5% resistance=220 package="2512 [SMD]"]
  J1 = Basic Servo
  Mod2 = KY-004 Key Switch Module [package="Breakout board"]
  Mod3 = KY-004 Key Switch Module [package="Breakout board"]
  Mod4 = KY-004 Key Switch Module [package="Breakout board"]

nets:
  VIN: Mod1.3V3, Part2.LV, Mod2.Vin, Mod3.Vin, Mod4.Vin
  VCC: Mod1.5V, Part1.VCC, Part2.HV, J1.vcc
  N1: Mod1.GPIO2, Part2.TX_LV
  N2: Mod1.GPIO3, Part2.RX_LV
  GND: Mod1.GND, Part1.GND, Part2.GND, R1.Pin_0, R9.Pin_0, J1.gnd, Mod2.-, Mod3.-, Mod4.-
  N3: Mod1.GPIO18, LED1.anode, J1.pulse
  N4: Mod1.GPIO5, LED2.anode
  N5: Mod1.GPIO6, R2.Pin_1
  N6: Mod1.GPIO19, R8.Pin_1
  N7: Mod1.GPIO26, R7.Pin_1
  N8: Part1.SDA, Part2.TX_HV
  N9: Part1.SCL, Part2.RX_HV
  N10: LED1.cathode, R1.Pin_1
  N11: R2.Pin_0, Mod2.S
  N12: LED2.cathode, R9.Pin_1
  N13: R7.Pin_0, Mod3.S
  N14: R8.Pin_0, Mod4.S

notes:
  5V
  3.3V

custom parts:
  LCD1602-I2C: A standard character display, usually with 2x16 characters. Comes in many colors with LCM1602 IIC attached.
  KY-004 Key Switch Module: Arduino Key Switch Module Keyes KY-004 is a push button that will output a high signal when pressed.
